# Fritzing sketch Bluetooth_Prototype (saved by Fritzing 0.9.3b)
breadboards: 1

parts:
  HC-05 = Bluetooth HC-05 Macho
  Composant2 = Arduino Mega 2560 (Rev3)
  part = Resistor [tolerance=±5% resistance=1k package=THT]
  R2 = Resistor [tolerance=±5% resistance=2k package=THT]
  DHT11 = KY-015 Temperature & Humidity Sensor Module [package="Breakout board"]
  Carte_ULN2003 = 28BYJ-48 Driver Module [part_number=ULN2003 package=THT]
  28BYJ-48_Unipolaire = 28BYJ-48 Stepper Motor [part_number=28BYJ-48]

nets:
  N1: HC-05.TXD, Composant2.D2_PWM
  N2: HC-05.RXD, part.Pin_1, R2.Pin_1
  VCC: HC-05.VCC, Composant2.5V, Carte_ULN2003.Vmotor
  GND: HC-05.GND, Composant2.GND, R2.Pin_0, DHT11.Vin, DHT11.-, Carte_ULN2003.GND
  N3: Composant2.D11_PWM, Composant2.D10_PWM, Composant2.D9_PWM, Composant2.D8_PWM, Carte_ULN2003.IN1, Carte_ULN2003.IN2, Carte_ULN2003.IN3, Carte_ULN2003.IN4
  N4: Composant2.D3_PWM, part.Pin_0
  N5: Composant2.D7_PWM, DHT11.S
  N6: Carte_ULN2003.blue-pin, 28BYJ-48_Unipolaire.blue-pin
  N7: Carte_ULN2003.pink-pin, 28BYJ-48_Unipolaire.pink-pin
  N8: Carte_ULN2003.yellow-pin, 28BYJ-48_Unipolaire.yellow-pin
  N9: Carte_ULN2003.orange-pin, 28BYJ-48_Unipolaire.orange-pin
  N10: Carte_ULN2003.red-pin, 28BYJ-48_Unipolaire.red-pin

notes:
  RX
  TX

custom parts:
  KY-015 Temperature & Humidity Sensor Module: KY-015 temperature and humidity sensor module, provides a low-latency serial interface to measure humidity and temperature.
  28BYJ-48 Driver Module: ULN2003 Driver Module for the 28BYJ-48 Unipolar Stepper Motor LED A - Blue wire - Bottom coil left LED B - Pink wire - Top coil left LED C - Yellow wire - Bottom coil right LED D - Orange wire - Top coil right Common rail - red Connector pins: blue - pink - yellow - orange - red Control pins - IN1 to IN4 Power pins - GND & Vmotor (5-12V) On/Off jumper (if removed, power to motor is cut).
  28BYJ-48 Stepper Motor: Unipolar Stepper Motor 28BYJ-48 Top coil - pink & orange Bottom coil - blue & yellow Common rail - red Connector pins: blue - pink - yellow - orange - red
